// Logisim project cpu.circ as structural Verilog: 1 circuit, main circuit main
module main (
  input  [31:0] RS_READ_VALUE,
  input  [31:0] RT_READ_VALUE,
  input  [31:0] INSTRUCTION,
  input  CLOCK,
  input  RESET,
  output [31:0] t0,
  output [31:0] t1,
  output [31:0] t2,
  output [31:0] t3,
  output [4:0] RS,
  output [4:0] RT,
  output [4:0] Write_Register,
  output [31:0] RD_WRITE_VALUE,
  output RD_WRITE_ENABLE,
  output [23:0] FETCH_ADDRESS
);

  wire and_out, comparator_1_lt, comparator_2_gt;

  Comparator #(.width(5), .mode("unsigned")) comparator_1 (
    .a(INSTRUCTION[20:16]), .b(5'b01100), .lt(comparator_1_lt));  // open: gt, eq
  Comparator #(.width(5), .mode("unsigned")) comparator_2 (
    .a(INSTRUCTION[20:16]), .b(5'b00111), .gt(comparator_2_gt));  // open: eq, lt
  and \and  (and_out, comparator_1_lt, comparator_2_gt);
  // alu_main ALU: pin names not known
  // mem_main MEM: pin names not known
  // regfile_main RegFile: pin names not known

  assign RS = INSTRUCTION[25:21];
  assign RT = INSTRUCTION[20:16];

  // Other names for the same wires on the sheet: clk = CLOCK; inst[31:0] = INSTRUCTION

  // Notes on the sheet:
  //   These are outputs/inputs from run.circ
  //   These are outputs to run.circ
  //   Feel free to move these components
endmodule
